// Logisim project ArithmaticUnit.circ as structural Verilog: 6 circuits, main circuit main
module main (
);

  wire and_1_out_17, and_1_out_18, and_1_out_19, and_1_out_20, and_1_out_21, and_1_out_22, and_1_out_23,
       and_1_out_24, multiplexer_1_out, multiplexer_2_out, multiplexer_3_out, multiplexer_4_out,
       multiplexer_5_out, multiplexer_6_out, multiplexer_7_out, multiplexer_8_out, multiplexer_9_out,
       multiplexer_10_out, multiplexer_11_out, multiplexer_12_out, multiplexer_13_out, multiplexer_14_out,
       multiplexer_15_out, multiplexer_16_out, or_1_out_17, or_1_out_18, or_1_out_19, or_1_out_20,
       or_1_out_21, or_1_out_22, or_1_out_23, or_1_out_24, undriven, undriven_2;

  eightBitAdder eightbitadder_1 ();  // open: Sub, Inc, in_3, in_4, in_5, in_6, A0_7, in_8, in_9, in_10, in_11, in_12, in_13, in_14, in_15, in_16, in_17, in_18, out_19, out_20, out_21, out_22, out_23, out_24, out_25, out_26, out_27
  And and_1 (
    .out_17(and_1_out_17), .out_18(and_1_out_18), .out_19(and_1_out_19), .out_20(and_1_out_20),
    .out_21(and_1_out_21), .out_22(and_1_out_22), .out_23(and_1_out_23), .out_24(and_1_out_24));  // open: in_1, in_2, in_3, in_4, in_5, in_6, in_7, in_8, in_9, in_10, in_11, in_12, in_13, in_14, in_15, in_16
  Or or_1 (
    .out_17(or_1_out_17), .out_18(or_1_out_18), .out_19(or_1_out_19), .out_20(or_1_out_20),
    .out_21(or_1_out_21), .out_22(or_1_out_22), .out_23(or_1_out_23), .out_24(or_1_out_24));  // open: in_1, in_2, in_3, in_4, in_5, in_6, in_7, in_8, in_9, in_10, in_11, in_12, in_13, in_14, in_15, in_16
  Multiplexer #(.enable("false")) multiplexer_1 (.out(multiplexer_1_out), .sel(undriven));  // open: in0, in1
  Multiplexer #(.enable("false")) multiplexer_2 (.out(multiplexer_2_out), .sel(undriven));  // open: in0, in1
  Multiplexer #(.enable("false")) multiplexer_3 (.out(multiplexer_3_out), .sel(undriven));  // open: in0, in1
  Multiplexer #(.enable("false")) multiplexer_4 (.out(multiplexer_4_out), .sel(undriven));  // open: in0, in1
  Multiplexer #(.enable("false")) multiplexer_5 (.out(multiplexer_5_out), .sel(undriven));  // open: in0, in1
  Multiplexer #(.enable("false")) multiplexer_6 (.out(multiplexer_6_out), .sel(undriven));  // open: in0, in1
  Multiplexer #(.enable("false")) multiplexer_7 (.out(multiplexer_7_out), .sel(undriven));  // open: in0, in1
  Multiplexer #(.enable("false")) multiplexer_8 (.out(multiplexer_8_out), .sel(undriven));  // open: in0, in1
  Multiplexer #(.enable("false")) multiplexer_9 (
    .in0(and_1_out_17), .in1(or_1_out_17), .out(multiplexer_9_out), .sel(undriven));
  Multiplexer #(.enable("false")) multiplexer_10 (
    .in0(and_1_out_18), .in1(or_1_out_18), .out(multiplexer_10_out), .sel(undriven));
  Multiplexer #(.enable("false")) multiplexer_11 (
    .in0(and_1_out_19), .in1(or_1_out_19), .out(multiplexer_11_out), .sel(undriven));
  Multiplexer #(.enable("false")) multiplexer_12 (
    .in0(and_1_out_20), .in1(or_1_out_20), .out(multiplexer_12_out), .sel(undriven));
  Multiplexer #(.enable("false")) multiplexer_13 (
    .in0(and_1_out_21), .in1(or_1_out_21), .out(multiplexer_13_out), .sel(undriven));
  Multiplexer #(.enable("false")) multiplexer_14 (
    .in0(and_1_out_22), .in1(or_1_out_22), .out(multiplexer_14_out), .sel(undriven));
  Multiplexer #(.enable("false")) multiplexer_15 (
    .in0(and_1_out_23), .in1(or_1_out_23), .out(multiplexer_15_out), .sel(undriven));
  Multiplexer #(.enable("false")) multiplexer_16 (
    .in0(and_1_out_24), .in1(or_1_out_24), .out(multiplexer_16_out), .sel(undriven));
  Multiplexer #(.enable("false")) multiplexer_17 (
    .in0(multiplexer_1_out), .in1(multiplexer_9_out), .sel(undriven_2));  // open: out
  Multiplexer #(.enable("false")) multiplexer_18 (
    .in0(multiplexer_2_out), .in1(multiplexer_10_out), .sel(undriven_2));  // open: out
  Multiplexer #(.enable("false")) multiplexer_19 (
    .in0(multiplexer_3_out), .in1(multiplexer_11_out), .sel(undriven_2));  // open: out
  Multiplexer #(.enable("false")) multiplexer_20 (
    .in0(multiplexer_4_out), .in1(multiplexer_12_out), .sel(undriven_2));  // open: out
  Multiplexer #(.enable("false")) multiplexer_21 (
    .in0(multiplexer_5_out), .in1(multiplexer_13_out), .sel(undriven_2));  // open: out
  Multiplexer #(.enable("false")) multiplexer_22 (
    .in0(multiplexer_6_out), .in1(multiplexer_14_out), .sel(undriven_2));  // open: out
  Multiplexer #(.enable("false")) multiplexer_23 (
    .in0(multiplexer_7_out), .in1(multiplexer_15_out), .sel(undriven_2));  // open: out
  Multiplexer #(.enable("false")) multiplexer_24 (
    .in0(multiplexer_8_out), .in1(multiplexer_16_out), .sel(undriven_2));  // open: out
endmodule

module eightBitAdder (
  input  Sub,
  input  Inc,
  input  in_3,
  input  in_4,
  input  in_5,
  input  in_6,
  input  A0_7,
  input  in_8,
  input  in_9,
  input  in_10,
  input  in_11,
  input  in_12,
  input  in_13,
  input  in_14,
  input  in_15,
  input  in_16,
  input  in_17,
  input  in_18,
  output out_19,
  output out_20,
  output out_21,
  output out_22,
  output out_23,
  output out_24,
  output out_25,
  output out_26,
  output out_27
);

  wire fulladder_1_c, fulladder_2_c, fulladder_3_c, fulladder_4_c, fulladder_5_c, fulladder_6_c,
       fulladder_7_c, xor_1_y1, xor_2_y1, xor_3_y1, xor_4_y1, xor_5_y1, xor_6_y1, xor_7_y1, xor_8_y1;

  XOR xor_1 (.X1(in_11), .X2(Sub), .Y1(xor_1_y1));
  XOR xor_2 (.X1(in_12), .X2(Sub), .Y1(xor_2_y1));
  XOR xor_3 (.X1(in_13), .X2(Sub), .Y1(xor_3_y1));
  XOR xor_4 (.X1(in_14), .X2(Sub), .Y1(xor_4_y1));
  XOR xor_5 (.X1(in_15), .X2(Sub), .Y1(xor_5_y1));
  XOR xor_6 (.X1(in_16), .X2(Sub), .Y1(xor_6_y1));
  XOR xor_7 (.X1(in_17), .X2(Sub), .Y1(xor_7_y1));
  XOR xor_8 (.X1(in_18), .X2(Sub), .Y1(xor_8_y1));
  fullAdder fulladder_1 (.A(in_3), .B(xor_1_y1), .Cin(Inc), .S(out_19), .C(fulladder_1_c));
  fullAdder fulladder_2 (.A(in_4), .B(xor_2_y1), .Cin(fulladder_1_c), .S(out_20), .C(fulladder_2_c));
  fullAdder fulladder_3 (.A(in_5), .B(xor_3_y1), .Cin(fulladder_2_c), .S(out_21), .C(fulladder_3_c));
  fullAdder fulladder_4 (.A(in_6), .B(xor_4_y1), .Cin(fulladder_3_c), .S(out_22), .C(fulladder_4_c));
  fullAdder fulladder_5 (.A(A0_7), .B(xor_5_y1), .Cin(fulladder_4_c), .S(out_23), .C(fulladder_5_c));
  fullAdder fulladder_6 (.A(in_8), .B(xor_6_y1), .Cin(fulladder_5_c), .S(out_24), .C(fulladder_6_c));
  fullAdder fulladder_7 (.A(in_9), .B(xor_7_y1), .Cin(fulladder_6_c), .S(out_25), .C(fulladder_7_c));
  fullAdder fulladder_8 (.A(in_10), .B(xor_8_y1), .Cin(fulladder_7_c), .S(out_26), .C(out_27));

  // Notes on the sheet:
  //   Need to Make subtract
  //   B0-7
endmodule

module fullAdder (
  input  A,
  input  B,
  input  Cin,
  output S,
  output C
);

  wire and_1_out, and_2_out, xor_1_y1;

  XOR xor_1 (.X1(A), .X2(B), .Y1(xor_1_y1));
  XOR xor_2 (.X1(xor_1_y1), .X2(Cin), .Y1(S));
  and and_1 (and_1_out, xor_1_y1, Cin);
  and and_2 (and_2_out, A, B);
  or or_1 (C, and_1_out, and_2_out);

  // Notes on the sheet:
  //   XOR Gates
endmodule

module XOR (
  input  X1,
  input  X2,
  output Y1
);

  wire and_1_out, and_2_out, not_1_out, not_2_out;

  not not_1 (not_1_out, X2);
  not not_2 (not_2_out, X1);
  and and_1 (and_1_out, X1, not_1_out);
  and and_2 (and_2_out, not_2_out, X2);
  or or_1 (Y1, and_1_out, and_2_out);
endmodule

module And (
  input  in_1,
  input  in_2,
  input  in_3,
  input  in_4,
  input  in_5,
  input  in_6,
  input  in_7,
  input  in_8,
  input  in_9,
  input  in_10,
  input  in_11,
  input  in_12,
  input  in_13,
  input  in_14,
  input  in_15,
  input  in_16,
  output out_17,
  output out_18,
  output out_19,
  output out_20,
  output out_21,
  output out_22,
  output out_23,
  output out_24
);

  and and_1 (out_17, in_1, in_9);
  and and_2 (out_18, in_2, in_10);
  and and_3 (out_19, in_3, in_11);
  and and_4 (out_20, in_4, in_12);
  and and_5 (out_21, in_5, in_13);
  and and_6 (out_22, in_6, in_14);
  and and_7 (out_23, in_7, in_15);
  and and_8 (out_24, in_8, in_16);
endmodule

module Or (
  input  in_1,
  input  in_2,
  input  in_3,
  input  in_4,
  input  in_5,
  input  in_6,
  input  in_7,
  input  in_8,
  input  in_9,
  input  in_10,
  input  in_11,
  input  in_12,
  input  in_13,
  input  in_14,
  input  in_15,
  input  in_16,
  output out_17,
  output out_18,
  output out_19,
  output out_20,
  output out_21,
  output out_22,
  output out_23,
  output out_24
);

  or or_1 (out_17, in_1, in_9);
  or or_2 (out_18, in_2, in_10);
  or or_3 (out_19, in_3, in_11);
  or or_4 (out_20, in_4, in_12);
  or or_5 (out_21, in_5, in_13);
  or or_6 (out_22, in_6, in_14);
  or or_7 (out_23, in_7, in_15);
  or or_8 (out_24, in_8, in_16);
endmodule
